# Fritzing sketch Helio_Tracker (saved by Fritzing 1.0.5)
breadboards: 1

parts:
  U1 = ESP32-38PinWide [part_number=ESP32-38PinWide]
  LED1 = LED - 3mm [color="Red (633nm)" current=0.030A package="3 mm [THT]"]
  R1 = Resistor [tolerance=±5% resistance=330 package="2010 [SMD]"]  # not connected
  R2 = PHOTOCELL [package=photocell-kit]
  R3 = Resistor [tolerance=±5% resistance=220 package="2010 [SMD]"]
  LED2 = LED - 3mm [color="White (6500K)" current=0.030A package="3 mm [THT]"]
  R4 = Resistor [tolerance=±5% resistance=330 package="2010 [SMD]"]
  LED3 = LED - 3mm [color="Green (570nm)" current=0.030A package="3 mm [THT]"]
  R5 = Resistor [tolerance=±5% resistance=330 package="2010 [SMD]"]
  R6 = PHOTOCELL [package=photocell-kit]
  R7 = Resistor [tolerance=±5% resistance=220 package="2010 [SMD]"]
  J1 = Basic Servo  # not connected
  元件1 = LCD1602-I2C

nets:
  N1: U1.GPIO34, R2.P$2, R3.Pin_0
  N2: U1.GPIO35, R6.P$2, R7.Pin_0
  N3: U1.GPIO11, LED1.cathode, R3.Pin_1, LED2.cathode, LED3.cathode, R7.Pin_1, 元件1.GND
  VIN: U1.VIN, R2.P$1, R6.P$1, 元件1.VCC
  N4: U1.GPIO16, R5.Pin_0
  N5: U1.GPIO17, R4.Pin_0
  N6: U1.GPIO21, 元件1.SDA
  N7: U1.GPIO22, 元件1.SCL
  N8: LED2.anode, R4.Pin_1
  N9: LED3.anode, R5.Pin_1

custom parts:
  ESP32-38PinWide: Generic 38-Pin ESP32 with wide format (only access to one side of pins on a breadboard) based on Stephen Lilley's HiLetgo ESP-WROOM-32 ESP32 ESP-32S Development Board.
  LCD1602-I2C: A standard character display, usually with 2x16 characters. Comes in many colors with LCM1602 IIC attached.
